// Logisim project Computer_8bits.circ as structural Verilog: 2 circuits, main circuit main
module main (
  input  in_1,
  input  in_2,
  input  in_3,
  input  in_4,
  input  in_5,
  input  in_6,
  input  in_7,
  input  in_8,
  input  EA,
  input  LA,
  input  CA,
  input  EB,
  input  LB,
  input  CB
);

  wire clock_1_out, register_1_bit0, register_1_bit1, register_1_bit2, register_1_bit3, register_1_bit4,
       register_1_bit5, register_1_bit6, register_1_bit7, register_2_bit0, register_2_bit1, register_2_bit2,
       register_2_bit3, register_2_bit4, register_2_bit5, register_2_bit6, register_2_bit7;

  DotMatrix #(.matrixcols(8), .matrixrows(1), .dotshape("circle")) dotmatrix_1 (
    .col0(in_1), .col1(in_2), .col2(in_3), .col3(in_4), .col4(in_5), .col5(in_6), .col6(in_7), .col7(in_8));
  Clock clock_1 (.out(clock_1_out));
  DotMatrix #(.inputtype("row"), .matrixcols(1), .matrixrows(8), .dotshape("circle")) dotmatrix_2 (
    .row0(register_1_bit7), .row1(register_1_bit6), .row2(register_1_bit5), .row3(register_1_bit4),
    .row4(register_1_bit3), .row5(register_1_bit2), .row6(register_1_bit1), .row7(register_1_bit0));
  DotMatrix #(.inputtype("row"), .matrixcols(1), .matrixrows(8), .dotshape("circle")) dotmatrix_3 (
    .row0(register_2_bit7), .row1(register_2_bit6), .row2(register_2_bit5), .row3(register_2_bit4),
    .row4(register_2_bit3), .row5(register_2_bit2), .row6(register_2_bit1), .row7(register_2_bit0));
  Register register_1 (
    .In0(in_1), .In1(in_2), .In2(in_3), .In3(in_4), .In4(in_5), .In5(in_6), .In6(in_7), .In7(in_8),
    .Out0(in_1), .Out1(in_2), .Out2(in_3), .Out3(in_4), .Out4(in_5), .Out5(in_6), .Out6(in_7), .Out7(in_8),
    .Clock(clock_1_out), .Load(LA), .Clear(CA), .Enable(EA), .Bit0(register_1_bit0), .Bit1(register_1_bit1),
    .Bit2(register_1_bit2), .Bit3(register_1_bit3), .Bit4(register_1_bit4), .Bit5(register_1_bit5),
    .Bit6(register_1_bit6), .Bit7(register_1_bit7));
  Register register_2 (
    .In0(in_1), .In1(in_2), .In2(in_3), .In3(in_4), .In4(in_5), .In5(in_6), .In6(in_7), .In7(in_8),
    .Out0(in_1), .Out1(in_2), .Out2(in_3), .Out3(in_4), .Out4(in_5), .Out5(in_6), .Out6(in_7), .Out7(in_8),
    .Clock(clock_1_out), .Load(LB), .Clear(CB), .Enable(EB), .Bit0(register_2_bit0), .Bit1(register_2_bit1),
    .Bit2(register_2_bit2), .Bit3(register_2_bit3), .Bit4(register_2_bit4), .Bit5(register_2_bit5),
    .Bit6(register_2_bit6), .Bit7(register_2_bit7));

  // Notes on the sheet:
  //   BUS
  //   Register A
  //   Register B
endmodule

module Register (
  input  Clock,
  input  Load,
  input  Clear,
  input  Enable,
  input  In0,
  input  In1,
  input  In2,
  input  In3,
  input  In4,
  input  In5,
  input  In6,
  input  In7,
  output Bit0,
  output Bit1,
  output Bit2,
  output Bit3,
  output Bit4,
  output Bit5,
  output Bit6,
  output Bit7,
  output Out0,
  output Out1,
  output Out2,
  output Out3,
  output Out4,
  output Out5,
  output Out6,
  output Out7
);

  Register_part #(.width(1)) register_1 (.D(In0), .en(Load), .Q(Bit0), .clk(Clock), .clr(Clear));
  Register_part #(.width(1)) register_2 (.D(In1), .en(Load), .Q(Bit1), .clk(Clock), .clr(Clear));
  Register_part #(.width(1)) register_3 (.D(In2), .en(Load), .Q(Bit2), .clk(Clock), .clr(Clear));
  Register_part #(.width(1)) register_4 (.D(In3), .en(Load), .Q(Bit3), .clk(Clock), .clr(Clear));
  Register_part #(.width(1)) register_5 (.D(In4), .en(Load), .Q(Bit4), .clk(Clock), .clr(Clear));
  Register_part #(.width(1)) register_6 (.D(In5), .en(Load), .Q(Bit5), .clk(Clock), .clr(Clear));
  Register_part #(.width(1)) register_7 (.D(In6), .en(Load), .Q(Bit6), .clk(Clock), .clr(Clear));
  Register_part #(.width(1)) register_8 (.D(In7), .en(Load), .Q(Bit7), .clk(Clock), .clr(Clear));
  assign Out0 = Enable ? Bit0 : 1'bz;  // Controlled_Buffer controlled_buffer_1
  assign Out1 = Enable ? Bit1 : 1'bz;  // Controlled_Buffer controlled_buffer_2
  assign Out2 = Enable ? Bit2 : 1'bz;  // Controlled_Buffer controlled_buffer_3
  assign Out3 = Enable ? Bit3 : 1'bz;  // Controlled_Buffer controlled_buffer_4
  assign Out4 = Enable ? Bit4 : 1'bz;  // Controlled_Buffer controlled_buffer_5
  assign Out5 = Enable ? Bit5 : 1'bz;  // Controlled_Buffer controlled_buffer_6
  assign Out6 = Enable ? Bit6 : 1'bz;  // Controlled_Buffer controlled_buffer_7
  assign Out7 = Enable ? Bit7 : 1'bz;  // Controlled_Buffer controlled_buffer_8
endmodule
