// Logisim project computer_8bits.circ as structural Verilog: 10 circuits, main circuit Processor
module Processor (
  input  Halt,
  input  IA,
  input  OA,
  input  CA,
  input  SE,
  input  OE,
  input  IB,
  input  OB,
  input  CB,
  input  IM,
  input  OM,
  input  CM,
  input  WRam,
  input  RRam,
  input  CRam,
  input  in_16,
  input  in_17,
  input  in_18,
  input  in_19,
  input  in_20,
  input  in_21,
  input  in_22,
  input  in_23,
  input  in_24,
  input  CI,
  input  PE,
  input  PJ,
  input  II,
  input  OI,
  input  CI_2
);

  wire alu_8_bits_1_co, alu_8_bits_1_s0, alu_8_bits_1_s1, alu_8_bits_1_s2, alu_8_bits_1_s3, alu_8_bits_1_s4,
       alu_8_bits_1_s5, alu_8_bits_1_s6, alu_8_bits_1_s7, and_1_out, clock_1_out, counter_8_bits_1_o0,
       counter_8_bits_1_o1, counter_8_bits_1_o2, counter_8_bits_1_o3, counter_8_bits_1_o4,
       counter_8_bits_1_o5, counter_8_bits_1_o6, counter_8_bits_1_o7, register_8_bits_1_b0,
       register_8_bits_1_b1, register_8_bits_1_b2, register_8_bits_1_b3, register_8_bits_1_b4,
       register_8_bits_1_b5, register_8_bits_1_b6, register_8_bits_1_b7, register_8_bits_1_o0,
       register_8_bits_1_o1, register_8_bits_1_o2, register_8_bits_1_o3, register_8_bits_1_o4,
       register_8_bits_1_o5, register_8_bits_1_o6, register_8_bits_1_o7, register_8_bits_2_b0,
       register_8_bits_2_b1, register_8_bits_2_b2, register_8_bits_2_b3, register_8_bits_2_b4,
       register_8_bits_2_b5, register_8_bits_2_b6, register_8_bits_2_b7, register_8_bits_2_o0,
       register_8_bits_2_o1, register_8_bits_2_o2, register_8_bits_2_o3, register_8_bits_2_o4,
       register_8_bits_2_o5, register_8_bits_2_o6, register_8_bits_2_o7, register_8_bits_3_b0,
       register_8_bits_3_b1, register_8_bits_3_b2, register_8_bits_3_b3, register_8_bits_3_b4,
       register_8_bits_3_b5, register_8_bits_3_b6, register_8_bits_3_b7, register_8_bits_4_b0,
       register_8_bits_4_b1, register_8_bits_4_b2, register_8_bits_4_b3, register_8_bits_4_b4,
       register_8_bits_4_b5, register_8_bits_4_b6, register_8_bits_4_b7, register_8_bits_4_o0,
       register_8_bits_4_o1, register_8_bits_4_o2, register_8_bits_4_o3, register_8_bits_4_o4,
       register_8_bits_4_o5, register_8_bits_4_o6, register_8_bits_4_o7, reverser_8_bits_1_s0,
       reverser_8_bits_1_s1, reverser_8_bits_1_s2, reverser_8_bits_1_s3, reverser_8_bits_1_s4,
       reverser_8_bits_1_s5, reverser_8_bits_1_s6, reverser_8_bits_1_s7;

  Clock clock_1 (.out(clock_1_out));
  and and_1 (and_1_out, clock_1_out, ~Halt);  // AND_Gate
  DotMatrix #(.inputtype("row"), .matrixcols(1), .matrixrows(8), .dotshape("circle")) dotmatrix_1 (
    .row0(register_8_bits_1_o7), .row1(register_8_bits_1_o6), .row2(register_8_bits_1_o5),
    .row3(register_8_bits_1_o4), .row4(register_8_bits_1_o3), .row5(register_8_bits_1_o2),
    .row6(register_8_bits_1_o1));  // open: row7
  DotMatrix #(.matrixcols(8), .matrixrows(1), .dotshape("circle")) dotmatrix_2 (
    .col0(register_8_bits_1_b7), .col1(register_8_bits_1_b6), .col2(register_8_bits_1_b5),
    .col3(register_8_bits_1_b4), .col4(register_8_bits_1_b3), .col5(register_8_bits_1_b2),
    .col6(register_8_bits_1_b1), .col7(register_8_bits_1_b0));
  DotMatrix #(.matrixcols(8), .matrixrows(1), .dotshape("circle")) dotmatrix_3 (
    .col0(counter_8_bits_1_o7), .col1(counter_8_bits_1_o6), .col2(counter_8_bits_1_o5),
    .col3(counter_8_bits_1_o4), .col4(counter_8_bits_1_o3), .col5(counter_8_bits_1_o2),
    .col6(counter_8_bits_1_o1), .col7(counter_8_bits_1_o0));
  Register_8_bits register_8_bits_1 (
    .I7(register_8_bits_1_o7), .I6(register_8_bits_1_o6), .I5(register_8_bits_1_o5),
    .I4(register_8_bits_1_o4), .I3(register_8_bits_1_o3), .I2(register_8_bits_1_o2),
    .I1(register_8_bits_1_o1), .I0(register_8_bits_1_o0), .O7(register_8_bits_1_o7),
    .O6(register_8_bits_1_o6), .O5(register_8_bits_1_o5), .O4(register_8_bits_1_o4),
    .O3(register_8_bits_1_o3), .O2(register_8_bits_1_o2), .O1(register_8_bits_1_o1),
    .O0(register_8_bits_1_o0), .Clock(and_1_out), .Load(IA), .Clear(CA), .Enable(OA),
    .B7(register_8_bits_1_b7), .B6(register_8_bits_1_b6), .B5(register_8_bits_1_b5),
    .B4(register_8_bits_1_b4), .B3(register_8_bits_1_b3), .B2(register_8_bits_1_b2),
    .B1(register_8_bits_1_b1), .B0(register_8_bits_1_b0));
  Counter_8_bits counter_8_bits_1 (
    .Enabled(PE), .Reset(CI), .Write(PJ), .Clock(and_1_out), .O7(counter_8_bits_1_o7),
    .O6(counter_8_bits_1_o6), .O5(counter_8_bits_1_o5), .O4(counter_8_bits_1_o4), .O3(counter_8_bits_1_o3),
    .O2(counter_8_bits_1_o2), .O1(counter_8_bits_1_o1), .O0(counter_8_bits_1_o0), .I7(register_8_bits_1_o7),
    .I6(register_8_bits_1_o6), .I5(register_8_bits_1_o5), .I4(register_8_bits_1_o4),
    .I3(register_8_bits_1_o3), .I2(register_8_bits_1_o2), .I1(register_8_bits_1_o1), .I0(register_8_bits_1_o0));
  LED led_1 (.in(alu_8_bits_1_co));
  DotMatrix #(.matrixcols(8), .matrixrows(1), .dotshape("circle")) dotmatrix_4 (
    .col0(alu_8_bits_1_s7), .col1(alu_8_bits_1_s6), .col2(alu_8_bits_1_s5), .col3(alu_8_bits_1_s4),
    .col4(alu_8_bits_1_s3), .col5(alu_8_bits_1_s2), .col6(alu_8_bits_1_s1), .col7(alu_8_bits_1_s0));
  ALU_8_bits alu_8_bits_1 (
    .E7(register_8_bits_1_o7), .E6(register_8_bits_1_o6), .E5(register_8_bits_1_o5),
    .E4(register_8_bits_1_o4), .E2(register_8_bits_1_o2), .E1(register_8_bits_1_o1),
    .E0(register_8_bits_1_o0), .Su(SE), .A7(register_8_bits_1_b7), .A6(register_8_bits_1_b6),
    .A5(register_8_bits_1_b5), .A4(register_8_bits_1_b4), .A3(register_8_bits_1_b3),
    .A2(register_8_bits_1_b2), .A1(register_8_bits_1_b1), .A0(register_8_bits_1_b0), .CO(alu_8_bits_1_co),
    .S7(alu_8_bits_1_s7), .S6(alu_8_bits_1_s6), .S5(alu_8_bits_1_s5), .S4(alu_8_bits_1_s4),
    .S3(alu_8_bits_1_s3), .S2(alu_8_bits_1_s2), .S1(alu_8_bits_1_s1), .S0(alu_8_bits_1_s0), .En(OE),
    .B7(register_8_bits_3_b7), .B6(register_8_bits_3_b6), .B5(register_8_bits_3_b5),
    .B4(register_8_bits_3_b4), .B3(register_8_bits_3_b3), .B2(register_8_bits_3_b2),
    .B1(register_8_bits_3_b1), .B0(register_8_bits_3_b0), .E3(register_8_bits_1_o3));
  DotMatrix #(.matrixcols(8), .matrixrows(1), .dotshape("circle")) dotmatrix_5 (
    .col0(register_8_bits_3_b7), .col1(register_8_bits_3_b6), .col2(register_8_bits_3_b5),
    .col3(register_8_bits_3_b4), .col4(register_8_bits_3_b3), .col5(register_8_bits_3_b2),
    .col6(register_8_bits_3_b1), .col7(register_8_bits_3_b0));
  DotMatrix #(.matrixcols(8), .matrixrows(1), .dotshape("circle")) dotmatrix_6 (
    .col0(reverser_8_bits_1_s0), .col1(reverser_8_bits_1_s1), .col2(reverser_8_bits_1_s2),
    .col3(reverser_8_bits_1_s3), .col4(reverser_8_bits_1_s4), .col5(reverser_8_bits_1_s5),
    .col6(reverser_8_bits_1_s6), .col7(reverser_8_bits_1_s7));
  Reverser_8_bits reverser_8_bits_1 (
    .S0(reverser_8_bits_1_s0), .S1(reverser_8_bits_1_s1), .S2(reverser_8_bits_1_s2),
    .S3(reverser_8_bits_1_s3), .S4(reverser_8_bits_1_s4), .S5(reverser_8_bits_1_s5),
    .S6(reverser_8_bits_1_s6), .S7(reverser_8_bits_1_s7), .E7(register_8_bits_2_b0),
    .E6(register_8_bits_2_b1), .E5(register_8_bits_2_b2), .E4(register_8_bits_2_b3),
    .E3(register_8_bits_2_b4), .E2(register_8_bits_2_b5), .E1(register_8_bits_2_b6), .E0(register_8_bits_2_b7));
  DotMatrix #(.inputtype("row"), .matrixcols(1), .matrixrows(8), .dotshape("circle")) dotmatrix_7 (
    .row0(register_8_bits_2_o0), .row1(register_8_bits_2_o1), .row2(register_8_bits_2_o2),
    .row3(register_8_bits_2_o3), .row4(register_8_bits_2_o4), .row5(register_8_bits_2_o5),
    .row6(register_8_bits_2_o6), .row7(register_8_bits_2_o7));
  Register_8_bits register_8_bits_2 (
    .I7(register_8_bits_1_o7), .I6(register_8_bits_1_o6), .I5(register_8_bits_1_o5),
    .I4(register_8_bits_1_o4), .I3(register_8_bits_1_o3), .I2(register_8_bits_1_o2),
    .I1(register_8_bits_1_o1), .I0(register_8_bits_1_o0), .O7(register_8_bits_2_o7),
    .O6(register_8_bits_2_o6), .O5(register_8_bits_2_o5), .O4(register_8_bits_2_o4),
    .O3(register_8_bits_2_o3), .O2(register_8_bits_2_o2), .O1(register_8_bits_2_o1),
    .O0(register_8_bits_2_o0), .Clock(and_1_out), .Load(II), .Clear(CI_2), .Enable(OI),
    .B7(register_8_bits_2_b7), .B6(register_8_bits_2_b6), .B5(register_8_bits_2_b5),
    .B4(register_8_bits_2_b4), .B3(register_8_bits_2_b3), .B2(register_8_bits_2_b2),
    .B1(register_8_bits_2_b1), .B0(register_8_bits_2_b0));
  Register_8_bits register_8_bits_3 (
    .I7(register_8_bits_1_o7), .I6(register_8_bits_1_o6), .I5(register_8_bits_1_o5),
    .I4(register_8_bits_1_o4), .I3(register_8_bits_1_o3), .I2(register_8_bits_1_o2),
    .I1(register_8_bits_1_o1), .I0(register_8_bits_1_o0), .O7(register_8_bits_1_o7),
    .O6(register_8_bits_1_o6), .O5(register_8_bits_1_o5), .O4(register_8_bits_1_o4),
    .O3(register_8_bits_1_o3), .O2(register_8_bits_1_o2), .O1(register_8_bits_1_o1),
    .O0(register_8_bits_1_o0), .Clock(and_1_out), .Load(IB), .Clear(CB), .Enable(OB),
    .B7(register_8_bits_3_b7), .B6(register_8_bits_3_b6), .B5(register_8_bits_3_b5),
    .B4(register_8_bits_3_b4), .B3(register_8_bits_3_b3), .B2(register_8_bits_3_b2),
    .B1(register_8_bits_3_b1), .B0(register_8_bits_3_b0));
  DotMatrix #(.matrixcols(8), .matrixrows(1), .dotshape("circle")) dotmatrix_8 (
    .col0(register_8_bits_4_b7), .col1(register_8_bits_4_b6), .col2(register_8_bits_4_b5),
    .col3(register_8_bits_4_b4), .col4(register_8_bits_4_b3), .col5(register_8_bits_4_b2),
    .col6(register_8_bits_4_b1), .col7(register_8_bits_4_b0));
  Register_8_bits register_8_bits_4 (
    .I7(register_8_bits_1_o7), .I6(register_8_bits_1_o6), .I5(register_8_bits_1_o5),
    .I4(register_8_bits_1_o4), .I3(register_8_bits_1_o3), .I2(register_8_bits_1_o2),
    .I1(register_8_bits_1_o1), .I0(register_8_bits_1_o0), .O7(register_8_bits_4_o7),
    .O6(register_8_bits_4_o6), .O5(register_8_bits_4_o5), .O4(register_8_bits_4_o4),
    .O3(register_8_bits_4_o3), .O2(register_8_bits_4_o2), .O1(register_8_bits_4_o1),
    .O0(register_8_bits_4_o0), .Clock(and_1_out), .Load(IM), .Clear(CM), .Enable(OM),
    .B7(register_8_bits_4_b7), .B6(register_8_bits_4_b6), .B5(register_8_bits_4_b5),
    .B4(register_8_bits_4_b4), .B3(register_8_bits_4_b3), .B2(register_8_bits_4_b2),
    .B1(register_8_bits_4_b1), .B0(register_8_bits_4_b0));
  SRAM_256_bytes sram_256_bytes_1 (
    .A7(register_8_bits_4_o7), .A6(register_8_bits_4_o6), .A5(register_8_bits_4_o5),
    .A4(register_8_bits_4_o4), .A3(register_8_bits_4_o3), .A2(register_8_bits_4_o2),
    .A1(register_8_bits_4_o1), .A0(register_8_bits_4_o0), .Write(WRam), .Read(RRam), .Clock(and_1_out),
    .Clear(CRam), .O7(register_8_bits_1_o7), .O6(register_8_bits_1_o6), .O5(register_8_bits_1_o5),
    .O4(register_8_bits_1_o4), .O3(register_8_bits_1_o3), .O2(register_8_bits_1_o2),
    .O1(register_8_bits_1_o1), .O0(register_8_bits_1_o0), .D7(register_8_bits_1_o7),
    .D6(register_8_bits_1_o6), .D5(register_8_bits_1_o5), .D4(register_8_bits_1_o4),
    .D3(register_8_bits_1_o3), .D2(register_8_bits_1_o2), .D1(register_8_bits_1_o1), .D0(register_8_bits_1_o0));
  assign register_8_bits_1_o7 = in_16 ? in_17 : 1'bz;  // Controlled_Buffer controlled_buffer_1
  assign register_8_bits_1_o6 = in_16 ? in_18 : 1'bz;  // Controlled_Buffer controlled_buffer_2
  assign register_8_bits_1_o5 = in_16 ? in_19 : 1'bz;  // Controlled_Buffer controlled_buffer_3
  assign register_8_bits_1_o4 = in_16 ? in_20 : 1'bz;  // Controlled_Buffer controlled_buffer_4
  assign register_8_bits_1_o3 = in_16 ? in_21 : 1'bz;  // Controlled_Buffer controlled_buffer_5
  assign register_8_bits_1_o2 = in_16 ? in_22 : 1'bz;  // Controlled_Buffer controlled_buffer_6
  assign register_8_bits_1_o1 = in_16 ? in_23 : 1'bz;  // Controlled_Buffer controlled_buffer_7
  assign register_8_bits_1_o0 = in_16 ? in_24 : 1'bz;  // Controlled_Buffer controlled_buffer_8

  // Notes on the sheet:
  //   Register A
  //   PC Register
  //   ALU
  //   Register B
  //   Instruction
  //   Register
  //   Memory
  //   Register
  //   RAM
endmodule

module Address_Decoder_4_bits (
  input  A3,
  input  Enable,
  input  A2,
  input  A1,
  input  A0,
  output DF,
  output DE,
  output DD,
  output DC,
  output DB,
  output DA,
  output D9,
  output D8,
  output D7,
  output D6,
  output D5,
  output D4,
  output D3,
  output D2,
  output D1,
  output D0
);

  wire and_1_out, and_2_out, and_3_out, and_4_out, and_5_out, and_6_out, and_7_out, and_8_out, and_9_out,
       and_10_out, and_11_out, and_12_out, and_13_out, and_14_out, and_15_out, and_16_out, not_1_out,
       not_2_out, not_3_out, not_4_out;

  not not_1 (not_1_out, A3);
  not not_2 (not_2_out, A2);
  not not_3 (not_3_out, A1);
  not not_4 (not_4_out, A0);
  and and_1 (and_1_out, not_1_out, not_2_out, not_3_out, not_4_out);
  and and_2 (and_2_out, not_1_out, not_2_out, not_3_out, A0);
  and and_3 (and_3_out, not_1_out, not_2_out, A1, not_4_out);
  and and_4 (and_4_out, not_1_out, not_2_out, A1, A0);
  and and_5 (and_5_out, not_1_out, A2, not_3_out, not_4_out);
  and and_6 (and_6_out, not_1_out, A2, not_3_out, A0);
  and and_7 (and_7_out, not_1_out, A2, A1, not_4_out);
  and and_8 (and_8_out, not_1_out, A2, A1, A0);
  and and_9 (and_9_out, A3, not_2_out, not_3_out, not_4_out);
  and and_10 (and_10_out, A3, not_2_out, not_3_out, A0);
  and and_11 (and_11_out, A3, not_2_out, A1, not_4_out);
  and and_12 (and_12_out, A3, not_2_out, A1, A0);
  and and_13 (and_13_out, A3, A2, not_3_out, not_4_out);
  and and_14 (and_14_out, A3, A2, not_3_out, A0);
  and and_15 (and_15_out, A3, A2, A1, not_4_out);
  and and_16 (and_16_out, A3, A2, A1, A0);
  assign DD = Enable ? and_14_out : 1'bz;  // Controlled_Buffer controlled_buffer_1
  assign DC = Enable ? and_13_out : 1'bz;  // Controlled_Buffer controlled_buffer_2
  assign DF = Enable ? and_16_out : 1'bz;  // Controlled_Buffer controlled_buffer_3
  assign DE = Enable ? and_15_out : 1'bz;  // Controlled_Buffer controlled_buffer_4
  assign DA = Enable ? and_11_out : 1'bz;  // Controlled_Buffer controlled_buffer_5
  assign D9 = Enable ? and_10_out : 1'bz;  // Controlled_Buffer controlled_buffer_6
  assign DB = Enable ? and_12_out : 1'bz;  // Controlled_Buffer controlled_buffer_7
  assign D8 = Enable ? and_9_out : 1'bz;  // Controlled_Buffer controlled_buffer_8
  assign D6 = Enable ? and_7_out : 1'bz;  // Controlled_Buffer controlled_buffer_9
  assign D7 = Enable ? and_8_out : 1'bz;  // Controlled_Buffer controlled_buffer_10
  assign D4 = Enable ? and_5_out : 1'bz;  // Controlled_Buffer controlled_buffer_11
  assign D5 = Enable ? and_6_out : 1'bz;  // Controlled_Buffer controlled_buffer_12
  assign D0 = Enable ? and_1_out : 1'bz;  // Controlled_Buffer controlled_buffer_13
  assign D2 = Enable ? and_3_out : 1'bz;  // Controlled_Buffer controlled_buffer_14
  assign D3 = Enable ? and_4_out : 1'bz;  // Controlled_Buffer controlled_buffer_15
  assign D1 = Enable ? and_2_out : 1'bz;  // Controlled_Buffer controlled_buffer_16
endmodule

module ALU_8_bits (
  input  Su,
  input  A7,
  input  A6,
  input  A5,
  input  A4,
  input  A3,
  input  A2,
  input  A1,
  input  A0,
  input  En,
  input  B7,
  input  B6,
  input  B5,
  input  B4,
  input  B3,
  input  B2,
  input  B1,
  input  B0,
  output CO,
  output S7,
  output S6,
  output S5,
  output S4,
  output S3,
  output S2,
  output S1,
  output S0,
  output E7,
  output E6,
  output E5,
  output E4,
  output E3,
  output E2,
  output E1,
  output E0
);

  wire full_adder_1_co, full_adder_2_co, full_adder_3_co, full_adder_4_co, full_adder_5_co, full_adder_6_co,
       full_adder_7_co, xor_1_out, xor_2_out, xor_3_out, xor_4_out, xor_5_out, xor_6_out, xor_7_out,
       xor_8_out;

  Full_adder full_adder_1 (.B(xor_7_out), .Ci(full_adder_2_co), .E(S1), .Co(full_adder_1_co), .A(A1));
  Full_adder full_adder_2 (.B(xor_8_out), .Ci(Su), .E(S0), .Co(full_adder_2_co), .A(A0));
  xor xor_1 (xor_1_out, Su, B7);
  Full_adder full_adder_3 (.B(xor_6_out), .Ci(full_adder_1_co), .E(S2), .Co(full_adder_3_co), .A(A2));
  xor xor_2 (xor_2_out, Su, B5);
  xor xor_3 (xor_3_out, Su, B6);
  Full_adder full_adder_4 (.B(xor_4_out), .Ci(full_adder_3_co), .E(S3), .Co(full_adder_4_co), .A(A3));
  xor xor_4 (xor_4_out, Su, B3);
  xor xor_5 (xor_5_out, Su, B4);
  Full_adder full_adder_5 (.B(xor_2_out), .Ci(full_adder_6_co), .E(S5), .Co(full_adder_5_co), .A(A5));
  Full_adder full_adder_6 (.B(xor_5_out), .Ci(full_adder_4_co), .E(S4), .Co(full_adder_6_co), .A(A4));
  xor xor_6 (xor_6_out, Su, B2);
  xor xor_7 (xor_7_out, Su, B1);
  Full_adder full_adder_7 (.B(xor_3_out), .Ci(full_adder_5_co), .E(S6), .Co(full_adder_7_co), .A(A6));
  xor xor_8 (xor_8_out, Su, B0);
  Full_adder full_adder_8 (.B(xor_1_out), .Ci(full_adder_7_co), .E(S7), .Co(CO), .A(A7));
  assign E7 = En ? S7 : 1'bz;  // Controlled_Buffer controlled_buffer_1
  assign E6 = En ? S6 : 1'bz;  // Controlled_Buffer controlled_buffer_2
  assign E5 = En ? S5 : 1'bz;  // Controlled_Buffer controlled_buffer_3
  assign E4 = En ? S4 : 1'bz;  // Controlled_Buffer controlled_buffer_4
  assign E3 = En ? S3 : 1'bz;  // Controlled_Buffer controlled_buffer_5
  assign E2 = En ? S2 : 1'bz;  // Controlled_Buffer controlled_buffer_6
  assign E1 = En ? S1 : 1'bz;  // Controlled_Buffer controlled_buffer_7
  assign E0 = En ? S0 : 1'bz;  // Controlled_Buffer controlled_buffer_8
endmodule

module Counter_8_bits (
  input  Clock,
  input  Enabled,
  input  Reset,
  input  Write,
  input  I7,
  input  I6,
  input  I5,
  input  I4,
  input  I3,
  input  I2,
  input  I1,
  input  I0,
  output O7,
  output O6,
  output O5,
  output O4,
  output O3,
  output O2,
  output O1,
  output O0
);

  wire and_1_out, and_2_out, and_3_out, and_4_out, and_5_out, and_6_out, and_7_out, and_8_out, and_9_out,
       and_10_out, and_11_out, and_12_out, and_13_out, and_14_out, and_15_out, and_16_out, and_17_out,
       j_k_ff_2_qn, j_k_ff_3_qn, j_k_ff_4_qn, j_k_ff_5_qn, j_k_ff_6_qn, j_k_ff_7_qn, j_k_ff_8_qn, or_1_out,
       or_2_out, or_3_out, or_4_out, or_5_out, or_6_out, or_7_out, or_8_out;

  and and_1 (and_1_out, Reset, Clock);
  J_K_Flip_Flop j_k_ff_1 (
    .J(1'b1), .clk(j_k_ff_2_qn), .K(1'b1), .Q(O7), .preset(and_3_out), .en(Enabled), .reset(or_1_out));  // open: Qn
  or or_1 (or_1_out, and_1_out, and_2_out);
  and and_2 (and_2_out, Write, ~I7, Clock);  // AND_Gate
  and and_3 (and_3_out, Write, I7, Clock);
  J_K_Flip_Flop j_k_ff_2 (
    .J(1'b1), .clk(j_k_ff_3_qn), .K(1'b1), .Q(O6), .Qn(j_k_ff_2_qn), .preset(and_4_out), .en(Enabled),
    .reset(or_2_out));
  or or_2 (or_2_out, and_1_out, and_5_out);
  and and_4 (and_4_out, Write, I6, Clock);
  and and_5 (and_5_out, Write, ~I6, Clock);  // AND_Gate
  J_K_Flip_Flop j_k_ff_3 (
    .J(1'b1), .clk(j_k_ff_4_qn), .K(1'b1), .Q(O5), .Qn(j_k_ff_3_qn), .preset(and_7_out), .en(Enabled),
    .reset(or_3_out));
  or or_3 (or_3_out, and_1_out, and_6_out);
  and and_6 (and_6_out, Write, ~I5, Clock);  // AND_Gate
  and and_7 (and_7_out, Write, I5, Clock);
  J_K_Flip_Flop j_k_ff_4 (
    .J(1'b1), .clk(j_k_ff_5_qn), .K(1'b1), .Q(O4), .Qn(j_k_ff_4_qn), .preset(and_9_out), .en(Enabled),
    .reset(or_4_out));
  or or_4 (or_4_out, and_1_out, and_8_out);
  and and_8 (and_8_out, Write, ~I4, Clock);  // AND_Gate
  and and_9 (and_9_out, Write, I4, Clock);
  J_K_Flip_Flop j_k_ff_5 (
    .J(1'b1), .clk(j_k_ff_6_qn), .K(1'b1), .Q(O3), .Qn(j_k_ff_5_qn), .preset(and_10_out), .en(Enabled),
    .reset(or_5_out));
  or or_5 (or_5_out, and_1_out, and_11_out);
  and and_10 (and_10_out, Write, I3, Clock);
  and and_11 (and_11_out, Write, ~I3, Clock);  // AND_Gate
  J_K_Flip_Flop j_k_ff_6 (
    .J(1'b1), .clk(j_k_ff_7_qn), .K(1'b1), .Q(O2), .Qn(j_k_ff_6_qn), .preset(and_13_out), .en(Enabled),
    .reset(or_6_out));
  or or_6 (or_6_out, and_1_out, and_12_out);
  and and_12 (and_12_out, Write, ~I2, Clock);  // AND_Gate
  and and_13 (and_13_out, Write, I2, Clock);
  J_K_Flip_Flop j_k_ff_7 (
    .J(1'b1), .clk(j_k_ff_8_qn), .K(1'b1), .Q(O1), .Qn(j_k_ff_7_qn), .preset(and_15_out), .en(Enabled),
    .reset(or_7_out));
  or or_7 (or_7_out, and_1_out, and_14_out);
  and and_14 (and_14_out, Write, ~I1, Clock);  // AND_Gate
  and and_15 (and_15_out, Write, I1, Clock);
  J_K_Flip_Flop j_k_ff_8 (
    .J(1'b1), .clk(Clock), .K(1'b1), .Q(O0), .Qn(j_k_ff_8_qn), .preset(and_17_out), .en(Enabled),
    .reset(or_8_out));
  or or_8 (or_8_out, and_1_out, and_16_out);
  and and_16 (and_16_out, Write, ~I0, Clock);  // AND_Gate
  and and_17 (and_17_out, Write, I0, Clock);
endmodule

module Full_adder (
  input  A,
  input  B,
  input  Ci,
  output E,
  output Co
);

  wire and_1_out, and_2_out, xor_1_out;

  xor xor_1 (xor_1_out, A, B);
  and and_1 (and_1_out, xor_1_out, Ci);
  and and_2 (and_2_out, A, B);
  xor xor_2 (E, xor_1_out, Ci);
  or or_1 (Co, and_1_out, and_2_out);
endmodule

module Grounder_4_bits (
  input  in_1,
  output G3,
  output G2,
  output G1,
  output G0
);

  assign G3 = in_1 ? 1'b0 : 1'bz;  // Controlled_Buffer controlled_buffer_1
  assign G1 = in_1 ? 1'b0 : 1'bz;  // Controlled_Buffer controlled_buffer_2
  assign G2 = in_1 ? 1'b0 : 1'bz;  // Controlled_Buffer controlled_buffer_3
  assign G0 = in_1 ? 1'b0 : 1'bz;  // Controlled_Buffer controlled_buffer_4
endmodule

module Register_8_bits (
  input  Clock,
  input  Load,
  input  Clear,
  input  Enable,
  input  I7,
  input  I6,
  input  I5,
  input  I4,
  input  I3,
  input  I2,
  input  I1,
  input  I0,
  output B7,
  output B6,
  output B5,
  output B4,
  output B3,
  output B2,
  output B1,
  output B0,
  output O7,
  output O6,
  output O5,
  output O4,
  output O3,
  output O2,
  output O1,
  output O0
);

  Register #(.width(1)) register_1 (.D(I7), .en(Load), .Q(B7), .clk(Clock), .clr(Clear));
  Register #(.width(1)) register_2 (.D(I6), .en(Load), .Q(B6), .clk(Clock), .clr(Clear));
  Register #(.width(1)) register_3 (.D(I5), .en(Load), .Q(B5), .clk(Clock), .clr(Clear));
  Register #(.width(1)) register_4 (.D(I4), .en(Load), .Q(B4), .clk(Clock), .clr(Clear));
  Register #(.width(1)) register_5 (.D(I3), .en(Load), .Q(B3), .clk(Clock), .clr(Clear));
  Register #(.width(1)) register_6 (.D(I2), .en(Load), .Q(B2), .clk(Clock), .clr(Clear));
  Register #(.width(1)) register_7 (.D(I1), .en(Load), .Q(B1), .clk(Clock), .clr(Clear));
  Register #(.width(1)) register_8 (.D(I0), .en(Load), .Q(B0), .clk(Clock), .clr(Clear));
  assign O7 = Enable ? B7 : 1'bz;  // Controlled_Buffer controlled_buffer_1
  assign O6 = Enable ? B6 : 1'bz;  // Controlled_Buffer controlled_buffer_2
  assign O5 = Enable ? B5 : 1'bz;  // Controlled_Buffer controlled_buffer_3
  assign O4 = Enable ? B4 : 1'bz;  // Controlled_Buffer controlled_buffer_4
  assign O3 = Enable ? B3 : 1'bz;  // Controlled_Buffer controlled_buffer_5
  assign O2 = Enable ? B2 : 1'bz;  // Controlled_Buffer controlled_buffer_6
  assign O1 = Enable ? B1 : 1'bz;  // Controlled_Buffer controlled_buffer_7
  assign O0 = Enable ? B0 : 1'bz;  // Controlled_Buffer controlled_buffer_8
endmodule

module Reverser_8_bits (
  input  E7,
  input  E6,
  input  E5,
  input  E4,
  input  E3,
  input  E2,
  input  E1,
  input  E0,
  output S0,
  output S1,
  output S2,
  output S3,
  output S4,
  output S5,
  output S6,
  output S7
);


  assign S0 = E0;
  assign S1 = E1;
  assign S2 = E2;
  assign S3 = E3;
  assign S4 = E4;
  assign S5 = E5;
  assign S6 = E6;
  assign S7 = E7;
endmodule

module SRAM_16_bytes (
  input  Write,
  input  Read,
  input  Clock,
  input  Clear,
  input  D7,
  input  D6,
  input  D5,
  input  D4,
  input  D3,
  input  D2,
  input  D1,
  input  D0,
  input  A3,
  input  A2,
  input  A1,
  input  A0,
  output O7,
  output O6,
  output O5,
  output O4,
  output O3,
  output O2,
  output O1,
  output O0
);

  wire address_decoder_4_bits_1_d0, address_decoder_4_bits_1_d1, address_decoder_4_bits_1_d2,
       address_decoder_4_bits_1_d3, address_decoder_4_bits_1_d4, address_decoder_4_bits_1_d5,
       address_decoder_4_bits_1_d6, address_decoder_4_bits_1_d7, address_decoder_4_bits_1_d8,
       address_decoder_4_bits_1_d9, address_decoder_4_bits_1_da, address_decoder_4_bits_1_db,
       address_decoder_4_bits_1_dc, address_decoder_4_bits_1_dd, address_decoder_4_bits_1_de,
       address_decoder_4_bits_1_df, and_1_out, and_2_out, and_3_out, and_4_out, and_5_out, and_6_out,
       and_7_out, and_8_out, and_9_out, and_10_out, and_11_out, and_12_out, and_13_out, and_14_out,
       and_15_out, and_16_out, and_17_out, and_18_out, and_19_out, and_20_out, and_21_out, and_22_out,
       and_23_out, and_24_out, and_25_out, and_26_out, and_27_out, and_28_out, and_29_out, and_30_out,
       and_31_out, and_32_out, register_8_bits_1_b0, register_8_bits_1_b1, register_8_bits_1_b2,
       register_8_bits_1_b3, register_8_bits_1_b4, register_8_bits_1_b5, register_8_bits_1_b6,
       register_8_bits_1_b7, register_8_bits_1_o0, register_8_bits_1_o1, register_8_bits_1_o2,
       register_8_bits_1_o3, register_8_bits_1_o4, register_8_bits_1_o5, register_8_bits_1_o6,
       register_8_bits_1_o7, register_8_bits_2_b0, register_8_bits_2_b1, register_8_bits_2_b2,
       register_8_bits_2_b3, register_8_bits_2_b4, register_8_bits_2_b5, register_8_bits_2_b6,
       register_8_bits_2_b7, register_8_bits_3_b0, register_8_bits_3_b1, register_8_bits_3_b2,
       register_8_bits_3_b3, register_8_bits_3_b4, register_8_bits_3_b5, register_8_bits_3_b6,
       register_8_bits_3_b7, register_8_bits_4_b0, register_8_bits_4_b1, register_8_bits_4_b2,
       register_8_bits_4_b3, register_8_bits_4_b4, register_8_bits_4_b5, register_8_bits_4_b6,
       register_8_bits_4_b7, register_8_bits_5_b0, register_8_bits_5_b1, register_8_bits_5_b2,
       register_8_bits_5_b3, register_8_bits_5_b4, register_8_bits_5_b5, register_8_bits_5_b6,
       register_8_bits_5_b7, register_8_bits_6_b0, register_8_bits_6_b1, register_8_bits_6_b2,
       register_8_bits_6_b3, register_8_bits_6_b4, register_8_bits_6_b5, register_8_bits_6_b6,
       register_8_bits_6_b7, register_8_bits_7_b0, register_8_bits_7_b1, register_8_bits_7_b2,
       register_8_bits_7_b3, register_8_bits_7_b4, register_8_bits_7_b5, register_8_bits_7_b6,
       register_8_bits_7_b7, register_8_bits_8_b0, register_8_bits_8_b1, register_8_bits_8_b2,
       register_8_bits_8_b3, register_8_bits_8_b4, register_8_bits_8_b5, register_8_bits_8_b6,
       register_8_bits_8_b7, register_8_bits_9_b0, register_8_bits_9_b1, register_8_bits_9_b2,
       register_8_bits_9_b3, register_8_bits_9_b4, register_8_bits_9_b5, register_8_bits_9_b6,
       register_8_bits_9_b7, register_8_bits_10_b0, register_8_bits_10_b1, register_8_bits_10_b2,
       register_8_bits_10_b3, register_8_bits_10_b4, register_8_bits_10_b5, register_8_bits_10_b6,
       register_8_bits_10_b7, register_8_bits_11_b0, register_8_bits_11_b1, register_8_bits_11_b2,
       register_8_bits_11_b3, register_8_bits_11_b4, register_8_bits_11_b5, register_8_bits_11_b6,
       register_8_bits_11_b7, register_8_bits_12_b0, register_8_bits_12_b1, register_8_bits_12_b2,
       register_8_bits_12_b3, register_8_bits_12_b4, register_8_bits_12_b5, register_8_bits_12_b6,
       register_8_bits_12_b7, register_8_bits_13_b0, register_8_bits_13_b1, register_8_bits_13_b2,
       register_8_bits_13_b3, register_8_bits_13_b4, register_8_bits_13_b5, register_8_bits_13_b6,
       register_8_bits_13_b7, register_8_bits_14_b0, register_8_bits_14_b1, register_8_bits_14_b2,
       register_8_bits_14_b3, register_8_bits_14_b4, register_8_bits_14_b5, register_8_bits_14_b6,
       register_8_bits_14_b7, register_8_bits_15_b0, register_8_bits_15_b1, register_8_bits_15_b2,
       register_8_bits_15_b3, register_8_bits_15_b4, register_8_bits_15_b5, register_8_bits_15_b6,
       register_8_bits_15_b7, register_8_bits_16_b0, register_8_bits_16_b1, register_8_bits_16_b2,
       register_8_bits_16_b3, register_8_bits_16_b4, register_8_bits_16_b5, register_8_bits_16_b6,
       register_8_bits_16_b7;

  Address_Decoder_4_bits address_decoder_4_bits_1 (
    .A3(A3), .A2(A2), .A1(A1), .A0(A0), .Enable(1'b1), .DF(address_decoder_4_bits_1_df),
    .DE(address_decoder_4_bits_1_de), .DD(address_decoder_4_bits_1_dd), .DC(address_decoder_4_bits_1_dc),
    .DB(address_decoder_4_bits_1_db), .DA(address_decoder_4_bits_1_da), .D9(address_decoder_4_bits_1_d9),
    .D8(address_decoder_4_bits_1_d8), .D7(address_decoder_4_bits_1_d7), .D6(address_decoder_4_bits_1_d6),
    .D5(address_decoder_4_bits_1_d5), .D4(address_decoder_4_bits_1_d4), .D3(address_decoder_4_bits_1_d3),
    .D2(address_decoder_4_bits_1_d2), .D1(address_decoder_4_bits_1_d1), .D0(address_decoder_4_bits_1_d0));
  and and_1 (and_1_out, Read, address_decoder_4_bits_1_d8);
  and and_2 (and_2_out, Write, address_decoder_4_bits_1_d8);
  and and_3 (and_3_out, Read, address_decoder_4_bits_1_d9);
  and and_4 (and_4_out, Write, address_decoder_4_bits_1_d9);
  and and_5 (and_5_out, Read, address_decoder_4_bits_1_da);
  and and_6 (and_6_out, Write, address_decoder_4_bits_1_da);
  and and_7 (and_7_out, Read, address_decoder_4_bits_1_db);
  and and_8 (and_8_out, Write, address_decoder_4_bits_1_db);
  and and_9 (and_9_out, Read, address_decoder_4_bits_1_dc);
  and and_10 (and_10_out, Write, address_decoder_4_bits_1_dc);
  and and_11 (and_11_out, Read, address_decoder_4_bits_1_dd);
  and and_12 (and_12_out, Write, address_decoder_4_bits_1_dd);
  and and_13 (and_13_out, Read, address_decoder_4_bits_1_de);
  and and_14 (and_14_out, Write, address_decoder_4_bits_1_de);
  and and_15 (and_15_out, Read, address_decoder_4_bits_1_df);
  and and_16 (and_16_out, Write, address_decoder_4_bits_1_df);
  Register_8_bits register_8_bits_1 (
    .I7(register_8_bits_1_o7), .I6(register_8_bits_1_o6), .I5(register_8_bits_1_o5),
    .I4(register_8_bits_1_o4), .I3(register_8_bits_1_o3), .I2(register_8_bits_1_o2),
    .I1(register_8_bits_1_o1), .I0(register_8_bits_1_o0), .O7(register_8_bits_1_o7),
    .O6(register_8_bits_1_o6), .O5(register_8_bits_1_o5), .O4(register_8_bits_1_o4),
    .O3(register_8_bits_1_o3), .O2(register_8_bits_1_o2), .O1(register_8_bits_1_o1),
    .O0(register_8_bits_1_o0), .Clock(Clock), .Load(and_2_out), .Clear(Clear), .Enable(and_1_out),
    .B7(register_8_bits_1_b7), .B6(register_8_bits_1_b6), .B5(register_8_bits_1_b5),
    .B4(register_8_bits_1_b4), .B3(register_8_bits_1_b3), .B2(register_8_bits_1_b2),
    .B1(register_8_bits_1_b1), .B0(register_8_bits_1_b0));
  Register_8_bits register_8_bits_2 (
    .I7(register_8_bits_1_o7), .I6(register_8_bits_1_o6), .I5(register_8_bits_1_o5),
    .I4(register_8_bits_1_o4), .I3(register_8_bits_1_o3), .I2(register_8_bits_1_o2),
    .I1(register_8_bits_1_o1), .I0(register_8_bits_1_o0), .O7(register_8_bits_1_o7),
    .O6(register_8_bits_1_o6), .O5(register_8_bits_1_o5), .O4(register_8_bits_1_o4),
    .O3(register_8_bits_1_o3), .O2(register_8_bits_1_o2), .O1(register_8_bits_1_o1),
    .O0(register_8_bits_1_o0), .Clock(Clock), .Load(and_4_out), .Clear(Clear), .Enable(and_3_out),
    .B7(register_8_bits_2_b7), .B6(register_8_bits_2_b6), .B5(register_8_bits_2_b5),
    .B4(register_8_bits_2_b4), .B3(register_8_bits_2_b3), .B2(register_8_bits_2_b2),
    .B1(register_8_bits_2_b1), .B0(register_8_bits_2_b0));
  Register_8_bits register_8_bits_3 (
    .I7(register_8_bits_1_o7), .I6(register_8_bits_1_o6), .I5(register_8_bits_1_o5),
    .I4(register_8_bits_1_o4), .I3(register_8_bits_1_o3), .I2(register_8_bits_1_o2),
    .I1(register_8_bits_1_o1), .I0(register_8_bits_1_o0), .O7(register_8_bits_1_o7),
    .O6(register_8_bits_1_o6), .O5(register_8_bits_1_o5), .O4(register_8_bits_1_o4),
    .O3(register_8_bits_1_o3), .O2(register_8_bits_1_o2), .O1(register_8_bits_1_o1),
    .O0(register_8_bits_1_o0), .Clock(Clock), .Load(and_6_out), .Clear(Clear), .Enable(and_5_out),
    .B7(register_8_bits_3_b7), .B6(register_8_bits_3_b6), .B5(register_8_bits_3_b5),
    .B4(register_8_bits_3_b4), .B3(register_8_bits_3_b3), .B2(register_8_bits_3_b2),
    .B1(register_8_bits_3_b1), .B0(register_8_bits_3_b0));
  Register_8_bits register_8_bits_4 (
    .I7(register_8_bits_1_o7), .I6(register_8_bits_1_o6), .I5(register_8_bits_1_o5),
    .I4(register_8_bits_1_o4), .I3(register_8_bits_1_o3), .I2(register_8_bits_1_o2),
    .I1(register_8_bits_1_o1), .I0(register_8_bits_1_o0), .O7(register_8_bits_1_o7),
    .O6(register_8_bits_1_o6), .O5(register_8_bits_1_o5), .O4(register_8_bits_1_o4),
    .O3(register_8_bits_1_o3), .O2(register_8_bits_1_o2), .O1(register_8_bits_1_o1),
    .O0(register_8_bits_1_o0), .Clock(Clock), .Load(and_8_out), .Clear(Clear), .Enable(and_7_out),
    .B7(register_8_bits_4_b7), .B6(register_8_bits_4_b6), .B5(register_8_bits_4_b5),
    .B4(register_8_bits_4_b4), .B3(register_8_bits_4_b3), .B2(register_8_bits_4_b2),
    .B1(register_8_bits_4_b1), .B0(register_8_bits_4_b0));
  Register_8_bits register_8_bits_5 (
    .I7(register_8_bits_1_o7), .I6(register_8_bits_1_o6), .I5(register_8_bits_1_o5),
    .I4(register_8_bits_1_o4), .I3(register_8_bits_1_o3), .I2(register_8_bits_1_o2),
    .I1(register_8_bits_1_o1), .I0(register_8_bits_1_o0), .O7(register_8_bits_1_o7),
    .O6(register_8_bits_1_o6), .O5(register_8_bits_1_o5), .O4(register_8_bits_1_o4),
    .O3(register_8_bits_1_o3), .O2(register_8_bits_1_o2), .O1(register_8_bits_1_o1),
    .O0(register_8_bits_1_o0), .Clock(Clock), .Load(and_10_out), .Clear(Clear), .Enable(and_9_out),
    .B7(register_8_bits_5_b7), .B6(register_8_bits_5_b6), .B5(register_8_bits_5_b5),
    .B4(register_8_bits_5_b4), .B3(register_8_bits_5_b3), .B2(register_8_bits_5_b2),
    .B1(register_8_bits_5_b1), .B0(register_8_bits_5_b0));
  Register_8_bits register_8_bits_6 (
    .I7(register_8_bits_1_o7), .I6(register_8_bits_1_o6), .I5(register_8_bits_1_o5),
    .I4(register_8_bits_1_o4), .I3(register_8_bits_1_o3), .I2(register_8_bits_1_o2),
    .I1(register_8_bits_1_o1), .I0(register_8_bits_1_o0), .O7(register_8_bits_1_o7),
    .O6(register_8_bits_1_o6), .O5(register_8_bits_1_o5), .O4(register_8_bits_1_o4),
    .O3(register_8_bits_1_o3), .O2(register_8_bits_1_o2), .O1(register_8_bits_1_o1),
    .O0(register_8_bits_1_o0), .Clock(Clock), .Load(and_12_out), .Clear(Clear), .Enable(and_11_out),
    .B7(register_8_bits_6_b7), .B6(register_8_bits_6_b6), .B5(register_8_bits_6_b5),
    .B4(register_8_bits_6_b4), .B3(register_8_bits_6_b3), .B2(register_8_bits_6_b2),
    .B1(register_8_bits_6_b1), .B0(register_8_bits_6_b0));
  Register_8_bits register_8_bits_7 (
    .I7(register_8_bits_1_o7), .I6(register_8_bits_1_o6), .I5(register_8_bits_1_o5),
    .I4(register_8_bits_1_o4), .I3(register_8_bits_1_o3), .I2(register_8_bits_1_o2),
    .I1(register_8_bits_1_o1), .I0(register_8_bits_1_o0), .O7(register_8_bits_1_o7),
    .O6(register_8_bits_1_o6), .O5(register_8_bits_1_o5), .O4(register_8_bits_1_o4),
    .O3(register_8_bits_1_o3), .O2(register_8_bits_1_o2), .O1(register_8_bits_1_o1),
    .O0(register_8_bits_1_o0), .Clock(Clock), .Load(and_14_out), .Clear(Clear), .Enable(and_13_out),
    .B7(register_8_bits_7_b7), .B6(register_8_bits_7_b6), .B5(register_8_bits_7_b5),
    .B4(register_8_bits_7_b4), .B3(register_8_bits_7_b3), .B2(register_8_bits_7_b2),
    .B1(register_8_bits_7_b1), .B0(register_8_bits_7_b0));
  Register_8_bits register_8_bits_8 (
    .I7(register_8_bits_1_o7), .I6(register_8_bits_1_o6), .I5(register_8_bits_1_o5),
    .I4(register_8_bits_1_o4), .I3(register_8_bits_1_o3), .I2(register_8_bits_1_o2),
    .I1(register_8_bits_1_o1), .I0(register_8_bits_1_o0), .O7(register_8_bits_1_o7),
    .O6(register_8_bits_1_o6), .O5(register_8_bits_1_o5), .O4(register_8_bits_1_o4),
    .O3(register_8_bits_1_o3), .O2(register_8_bits_1_o2), .O1(register_8_bits_1_o1),
    .O0(register_8_bits_1_o0), .Clock(Clock), .Load(and_16_out), .Clear(Clear), .Enable(and_15_out),
    .B7(register_8_bits_8_b7), .B6(register_8_bits_8_b6), .B5(register_8_bits_8_b5),
    .B4(register_8_bits_8_b4), .B3(register_8_bits_8_b3), .B2(register_8_bits_8_b2),
    .B1(register_8_bits_8_b1), .B0(register_8_bits_8_b0));
  assign O7 = Read ? register_8_bits_1_o7 : 1'bz;  // Controlled_Buffer controlled_buffer_1
  assign O6 = Read ? register_8_bits_1_o6 : 1'bz;  // Controlled_Buffer controlled_buffer_2
  DotMatrix #(.inputtype("row"), .matrixcols(1), .matrixrows(8), .dotshape("circle")) dotmatrix_1 (
    .row0(register_8_bits_1_b0), .row1(register_8_bits_1_b1), .row2(register_8_bits_1_b2),
    .row3(register_8_bits_1_b3), .row4(register_8_bits_1_b4), .row5(register_8_bits_1_b5),
    .row6(register_8_bits_1_b6), .row7(register_8_bits_1_b7));
  DotMatrix #(.inputtype("row"), .matrixcols(1), .matrixrows(8), .dotshape("circle")) dotmatrix_2 (
    .row0(register_8_bits_2_b0), .row1(register_8_bits_2_b1), .row2(register_8_bits_2_b2),
    .row3(register_8_bits_2_b3), .row4(register_8_bits_2_b4), .row5(register_8_bits_2_b5),
    .row6(register_8_bits_2_b6), .row7(register_8_bits_2_b7));
  DotMatrix #(.inputtype("row"), .matrixcols(1), .matrixrows(8), .dotshape("circle")) dotmatrix_3 (
    .row0(register_8_bits_3_b0), .row1(register_8_bits_3_b1), .row2(register_8_bits_3_b2),
    .row3(register_8_bits_3_b3), .row4(register_8_bits_3_b4), .row5(register_8_bits_3_b5),
    .row6(register_8_bits_3_b6), .row7(register_8_bits_3_b7));
  DotMatrix #(.inputtype("row"), .matrixcols(1), .matrixrows(8), .dotshape("circle")) dotmatrix_4 (
    .row0(register_8_bits_4_b0), .row1(register_8_bits_4_b1), .row2(register_8_bits_4_b2),
    .row3(register_8_bits_4_b3), .row4(register_8_bits_4_b4), .row5(register_8_bits_4_b5),
    .row6(register_8_bits_4_b6), .row7(register_8_bits_4_b7));
  DotMatrix #(.inputtype("row"), .matrixcols(1), .matrixrows(8), .dotshape("circle")) dotmatrix_5 (
    .row0(register_8_bits_5_b0), .row1(register_8_bits_5_b1), .row2(register_8_bits_5_b2),
    .row3(register_8_bits_5_b3), .row4(register_8_bits_5_b4), .row5(register_8_bits_5_b5),
    .row6(register_8_bits_5_b6), .row7(register_8_bits_5_b7));
  DotMatrix #(.inputtype("row"), .matrixcols(1), .matrixrows(8), .dotshape("circle")) dotmatrix_6 (
    .row0(register_8_bits_6_b0), .row1(register_8_bits_6_b1), .row2(register_8_bits_6_b2),
    .row3(register_8_bits_6_b3), .row4(register_8_bits_6_b4), .row5(register_8_bits_6_b5),
    .row6(register_8_bits_6_b6), .row7(register_8_bits_6_b7));
  DotMatrix #(.inputtype("row"), .matrixcols(1), .matrixrows(8), .dotshape("circle")) dotmatrix_7 (
    .row0(register_8_bits_7_b0), .row1(register_8_bits_7_b1), .row2(register_8_bits_7_b2),
    .row3(register_8_bits_7_b3), .row4(register_8_bits_7_b4), .row5(register_8_bits_7_b5),
    .row6(register_8_bits_7_b6), .row7(register_8_bits_7_b7));
  DotMatrix #(.inputtype("row"), .matrixcols(1), .matrixrows(8), .dotshape("circle")) dotmatrix_8 (
    .row0(register_8_bits_8_b0), .row1(register_8_bits_8_b1), .row2(register_8_bits_8_b2),
    .row3(register_8_bits_8_b3), .row4(register_8_bits_8_b4), .row5(register_8_bits_8_b5),
    .row6(register_8_bits_8_b6), .row7(register_8_bits_8_b7));
  assign O2 = Read ? register_8_bits_1_o2 : 1'bz;  // Controlled_Buffer controlled_buffer_3
  assign O4 = Read ? register_8_bits_1_o4 : 1'bz;  // Controlled_Buffer controlled_buffer_4
  assign O5 = Read ? register_8_bits_1_o5 : 1'bz;  // Controlled_Buffer controlled_buffer_5
  assign O3 = Read ? register_8_bits_1_o3 : 1'bz;  // Controlled_Buffer controlled_buffer_6
  assign O0 = Read ? register_8_bits_1_o0 : 1'bz;  // Controlled_Buffer controlled_buffer_7
  assign O1 = Read ? register_8_bits_1_o1 : 1'bz;  // Controlled_Buffer controlled_buffer_8
  assign register_8_bits_1_o7 = Write ? D7 : 1'bz;  // Controlled_Buffer controlled_buffer_9
  DotMatrix #(.inputtype("row"), .matrixcols(1), .matrixrows(8), .dotshape("circle")) dotmatrix_9 (
    .row0(register_8_bits_9_b7), .row1(register_8_bits_9_b6), .row2(register_8_bits_9_b5),
    .row3(register_8_bits_9_b4), .row4(register_8_bits_9_b3), .row5(register_8_bits_9_b2),
    .row6(register_8_bits_9_b1), .row7(register_8_bits_9_b0));
  DotMatrix #(.inputtype("row"), .matrixcols(1), .matrixrows(8), .dotshape("circle")) dotmatrix_10 (
    .row0(register_8_bits_10_b7), .row1(register_8_bits_10_b6), .row2(register_8_bits_10_b5),
    .row3(register_8_bits_10_b4), .row4(register_8_bits_10_b3), .row5(register_8_bits_10_b2),
    .row6(register_8_bits_10_b1), .row7(register_8_bits_10_b0));
  DotMatrix #(.inputtype("row"), .matrixcols(1), .matrixrows(8), .dotshape("circle")) dotmatrix_11 (
    .row0(register_8_bits_11_b7), .row1(register_8_bits_11_b6), .row2(register_8_bits_11_b5),
    .row3(register_8_bits_11_b4), .row4(register_8_bits_11_b3), .row5(register_8_bits_11_b2),
    .row6(register_8_bits_11_b1), .row7(register_8_bits_11_b0));
  DotMatrix #(.inputtype("row"), .matrixcols(1), .matrixrows(8), .dotshape("circle")) dotmatrix_12 (
    .row0(register_8_bits_12_b7), .row1(register_8_bits_12_b6), .row2(register_8_bits_12_b5),
    .row3(register_8_bits_12_b4), .row4(register_8_bits_12_b3), .row5(register_8_bits_12_b2),
    .row6(register_8_bits_12_b1), .row7(register_8_bits_12_b0));
  DotMatrix #(.inputtype("row"), .matrixcols(1), .matrixrows(8), .dotshape("circle")) dotmatrix_13 (
    .row0(register_8_bits_13_b7), .row1(register_8_bits_13_b6), .row2(register_8_bits_13_b5),
    .row3(register_8_bits_13_b4), .row4(register_8_bits_13_b3), .row5(register_8_bits_13_b2),
    .row6(register_8_bits_13_b1), .row7(register_8_bits_13_b0));
  DotMatrix #(.inputtype("row"), .matrixcols(1), .matrixrows(8), .dotshape("circle")) dotmatrix_14 (
    .row0(register_8_bits_14_b7), .row1(register_8_bits_14_b6), .row2(register_8_bits_14_b5),
    .row3(register_8_bits_14_b4), .row4(register_8_bits_14_b3), .row5(register_8_bits_14_b2),
    .row6(register_8_bits_14_b1), .row7(register_8_bits_14_b0));
  DotMatrix #(.inputtype("row"), .matrixcols(1), .matrixrows(8), .dotshape("circle")) dotmatrix_15 (
    .row0(register_8_bits_15_b7), .row1(register_8_bits_15_b6), .row2(register_8_bits_15_b5),
    .row3(register_8_bits_15_b4), .row4(register_8_bits_15_b3), .row5(register_8_bits_15_b2),
    .row6(register_8_bits_15_b1), .row7(register_8_bits_15_b0));
  DotMatrix #(.inputtype("row"), .matrixcols(1), .matrixrows(8), .dotshape("circle")) dotmatrix_16 (
    .row0(register_8_bits_16_b7), .row1(register_8_bits_16_b6), .row2(register_8_bits_16_b5),
    .row3(register_8_bits_16_b4), .row4(register_8_bits_16_b3), .row5(register_8_bits_16_b2),
    .row6(register_8_bits_16_b1), .row7(register_8_bits_16_b0));
  assign register_8_bits_1_o3 = Write ? D3 : 1'bz;  // Controlled_Buffer controlled_buffer_10
  assign register_8_bits_1_o4 = Write ? D4 : 1'bz;  // Controlled_Buffer controlled_buffer_11
  assign register_8_bits_1_o6 = Write ? D6 : 1'bz;  // Controlled_Buffer controlled_buffer_12
  assign register_8_bits_1_o5 = Write ? D5 : 1'bz;  // Controlled_Buffer controlled_buffer_13
  Register_8_bits register_8_bits_9 (
    .I7(register_8_bits_1_o7), .I6(register_8_bits_1_o6), .I5(register_8_bits_1_o5),
    .I4(register_8_bits_1_o4), .I3(register_8_bits_1_o3), .I2(register_8_bits_1_o2),
    .I1(register_8_bits_1_o1), .I0(register_8_bits_1_o0), .O7(register_8_bits_1_o7),
    .O6(register_8_bits_1_o6), .O5(register_8_bits_1_o5), .O4(register_8_bits_1_o4),
    .O3(register_8_bits_1_o3), .O2(register_8_bits_1_o2), .O1(register_8_bits_1_o1),
    .O0(register_8_bits_1_o0), .Clock(Clock), .Load(and_17_out), .Clear(Clear), .Enable(and_18_out),
    .B7(register_8_bits_9_b7), .B6(register_8_bits_9_b6), .B5(register_8_bits_9_b5),
    .B4(register_8_bits_9_b4), .B3(register_8_bits_9_b3), .B2(register_8_bits_9_b2),
    .B1(register_8_bits_9_b1), .B0(register_8_bits_9_b0));
  Register_8_bits register_8_bits_10 (
    .I7(register_8_bits_1_o7), .I6(register_8_bits_1_o6), .I5(register_8_bits_1_o5),
    .I4(register_8_bits_1_o4), .I3(register_8_bits_1_o3), .I2(register_8_bits_1_o2),
    .I1(register_8_bits_1_o1), .I0(register_8_bits_1_o0), .O7(register_8_bits_1_o7),
    .O6(register_8_bits_1_o6), .O5(register_8_bits_1_o5), .O4(register_8_bits_1_o4),
    .O3(register_8_bits_1_o3), .O2(register_8_bits_1_o2), .O1(register_8_bits_1_o1),
    .O0(register_8_bits_1_o0), .Clock(Clock), .Load(and_19_out), .Clear(Clear), .Enable(and_20_out),
    .B7(register_8_bits_10_b7), .B6(register_8_bits_10_b6), .B5(register_8_bits_10_b5),
    .B4(register_8_bits_10_b4), .B3(register_8_bits_10_b3), .B2(register_8_bits_10_b2),
    .B1(register_8_bits_10_b1), .B0(register_8_bits_10_b0));
  Register_8_bits register_8_bits_11 (
    .I7(register_8_bits_1_o7), .I6(register_8_bits_1_o6), .I5(register_8_bits_1_o5),
    .I4(register_8_bits_1_o4), .I3(register_8_bits_1_o3), .I2(register_8_bits_1_o2),
    .I1(register_8_bits_1_o1), .I0(register_8_bits_1_o0), .O7(register_8_bits_1_o7),
    .O6(register_8_bits_1_o6), .O5(register_8_bits_1_o5), .O4(register_8_bits_1_o4),
    .O3(register_8_bits_1_o3), .O2(register_8_bits_1_o2), .O1(register_8_bits_1_o1),
    .O0(register_8_bits_1_o0), .Clock(Clock), .Load(and_21_out), .Clear(Clear), .Enable(and_22_out),
    .B7(register_8_bits_11_b7), .B6(register_8_bits_11_b6), .B5(register_8_bits_11_b5),
    .B4(register_8_bits_11_b4), .B3(register_8_bits_11_b3), .B2(register_8_bits_11_b2),
    .B1(register_8_bits_11_b1), .B0(register_8_bits_11_b0));
  Register_8_bits register_8_bits_12 (
    .I7(register_8_bits_1_o7), .I6(register_8_bits_1_o6), .I5(register_8_bits_1_o5),
    .I4(register_8_bits_1_o4), .I3(register_8_bits_1_o3), .I2(register_8_bits_1_o2),
    .I1(register_8_bits_1_o1), .I0(register_8_bits_1_o0), .O7(register_8_bits_1_o7),
    .O6(register_8_bits_1_o6), .O5(register_8_bits_1_o5), .O4(register_8_bits_1_o4),
    .O3(register_8_bits_1_o3), .O2(register_8_bits_1_o2), .O1(register_8_bits_1_o1),
    .O0(register_8_bits_1_o0), .Clock(Clock), .Load(and_23_out), .Clear(Clear), .Enable(and_24_out),
    .B7(register_8_bits_12_b7), .B6(register_8_bits_12_b6), .B5(register_8_bits_12_b5),
    .B4(register_8_bits_12_b4), .B3(register_8_bits_12_b3), .B2(register_8_bits_12_b2),
    .B1(register_8_bits_12_b1), .B0(register_8_bits_12_b0));
  Register_8_bits register_8_bits_13 (
    .I7(register_8_bits_1_o7), .I6(register_8_bits_1_o6), .I5(register_8_bits_1_o5),
    .I4(register_8_bits_1_o4), .I3(register_8_bits_1_o3), .I2(register_8_bits_1_o2),
    .I1(register_8_bits_1_o1), .I0(register_8_bits_1_o0), .O7(register_8_bits_1_o7),
    .O6(register_8_bits_1_o6), .O5(register_8_bits_1_o5), .O4(register_8_bits_1_o4),
    .O3(register_8_bits_1_o3), .O2(register_8_bits_1_o2), .O1(register_8_bits_1_o1),
    .O0(register_8_bits_1_o0), .Clock(Clock), .Load(and_25_out), .Clear(Clear), .Enable(and_26_out),
    .B7(register_8_bits_13_b7), .B6(register_8_bits_13_b6), .B5(register_8_bits_13_b5),
    .B4(register_8_bits_13_b4), .B3(register_8_bits_13_b3), .B2(register_8_bits_13_b2),
    .B1(register_8_bits_13_b1), .B0(register_8_bits_13_b0));
  Register_8_bits register_8_bits_14 (
    .I7(register_8_bits_1_o7), .I6(register_8_bits_1_o6), .I5(register_8_bits_1_o5),
    .I4(register_8_bits_1_o4), .I3(register_8_bits_1_o3), .I2(register_8_bits_1_o2),
    .I1(register_8_bits_1_o1), .I0(register_8_bits_1_o0), .O7(register_8_bits_1_o7),
    .O6(register_8_bits_1_o6), .O5(register_8_bits_1_o5), .O4(register_8_bits_1_o4),
    .O3(register_8_bits_1_o3), .O2(register_8_bits_1_o2), .O1(register_8_bits_1_o1),
    .O0(register_8_bits_1_o0), .Clock(Clock), .Load(and_27_out), .Clear(Clear), .Enable(and_28_out),
    .B7(register_8_bits_14_b7), .B6(register_8_bits_14_b6), .B5(register_8_bits_14_b5),
    .B4(register_8_bits_14_b4), .B3(register_8_bits_14_b3), .B2(register_8_bits_14_b2),
    .B1(register_8_bits_14_b1), .B0(register_8_bits_14_b0));
  Register_8_bits register_8_bits_15 (
    .I7(register_8_bits_1_o7), .I6(register_8_bits_1_o6), .I5(register_8_bits_1_o5),
    .I4(register_8_bits_1_o4), .I3(register_8_bits_1_o3), .I2(register_8_bits_1_o2),
    .I1(register_8_bits_1_o1), .I0(register_8_bits_1_o0), .O7(register_8_bits_1_o7),
    .O6(register_8_bits_1_o6), .O5(register_8_bits_1_o5), .O4(register_8_bits_1_o4),
    .O3(register_8_bits_1_o3), .O2(register_8_bits_1_o2), .O1(register_8_bits_1_o1),
    .O0(register_8_bits_1_o0), .Clock(Clock), .Load(and_29_out), .Clear(Clear), .Enable(and_30_out),
    .B7(register_8_bits_15_b7), .B6(register_8_bits_15_b6), .B5(register_8_bits_15_b5),
    .B4(register_8_bits_15_b4), .B3(register_8_bits_15_b3), .B2(register_8_bits_15_b2),
    .B1(register_8_bits_15_b1), .B0(register_8_bits_15_b0));
  Register_8_bits register_8_bits_16 (
    .I7(register_8_bits_1_o7), .I6(register_8_bits_1_o6), .I5(register_8_bits_1_o5),
    .I4(register_8_bits_1_o4), .I3(register_8_bits_1_o3), .I2(register_8_bits_1_o2),
    .I1(register_8_bits_1_o1), .I0(register_8_bits_1_o0), .O7(register_8_bits_1_o7),
    .O6(register_8_bits_1_o6), .O5(register_8_bits_1_o5), .O4(register_8_bits_1_o4),
    .O3(register_8_bits_1_o3), .O2(register_8_bits_1_o2), .O1(register_8_bits_1_o1),
    .O0(register_8_bits_1_o0), .Clock(Clock), .Load(and_31_out), .Clear(Clear), .Enable(and_32_out),
    .B7(register_8_bits_16_b7), .B6(register_8_bits_16_b6), .B5(register_8_bits_16_b5),
    .B4(register_8_bits_16_b4), .B3(register_8_bits_16_b3), .B2(register_8_bits_16_b2),
    .B1(register_8_bits_16_b1), .B0(register_8_bits_16_b0));
  assign register_8_bits_1_o0 = Write ? D0 : 1'bz;  // Controlled_Buffer controlled_buffer_14
  assign register_8_bits_1_o2 = Write ? D2 : 1'bz;  // Controlled_Buffer controlled_buffer_15
  assign register_8_bits_1_o1 = Write ? D1 : 1'bz;  // Controlled_Buffer controlled_buffer_16
  and and_17 (and_17_out, Write, address_decoder_4_bits_1_d0);
  and and_18 (and_18_out, Read, address_decoder_4_bits_1_d0);
  and and_19 (and_19_out, Write, address_decoder_4_bits_1_d1);
  and and_20 (and_20_out, Read, address_decoder_4_bits_1_d1);
  and and_21 (and_21_out, Write, address_decoder_4_bits_1_d2);
  and and_22 (and_22_out, Read, address_decoder_4_bits_1_d2);
  and and_23 (and_23_out, Write, address_decoder_4_bits_1_d7);
  and and_24 (and_24_out, Read, address_decoder_4_bits_1_d7);
  and and_25 (and_25_out, Write, address_decoder_4_bits_1_d3);
  and and_26 (and_26_out, Read, address_decoder_4_bits_1_d3);
  and and_27 (and_27_out, Write, address_decoder_4_bits_1_d4);
  and and_28 (and_28_out, Read, address_decoder_4_bits_1_d4);
  and and_29 (and_29_out, Write, address_decoder_4_bits_1_d5);
  and and_30 (and_30_out, Read, address_decoder_4_bits_1_d5);
  and and_31 (and_31_out, Write, address_decoder_4_bits_1_d6);
  and and_32 (and_32_out, Read, address_decoder_4_bits_1_d6);
endmodule

module SRAM_256_bytes (
  input  Write,
  input  Read,
  input  Clock,
  input  Clear,
  input  D7,
  input  D6,
  input  D5,
  input  D4,
  input  D3,
  input  D2,
  input  D1,
  input  D0,
  input  A7,
  input  A6,
  input  A5,
  input  A4,
  input  A3,
  input  A2,
  input  A1,
  input  A0,
  output O7,
  output O6,
  output O5,
  output O4,
  output O3,
  output O2,
  output O1,
  output O0
);

  wire address_decoder_4_bits_1_d0, address_decoder_4_bits_1_d1, address_decoder_4_bits_1_d2,
       address_decoder_4_bits_1_d3, address_decoder_4_bits_1_d4, address_decoder_4_bits_1_d5,
       address_decoder_4_bits_1_d6, address_decoder_4_bits_1_d7, address_decoder_4_bits_1_d8,
       address_decoder_4_bits_1_d9, address_decoder_4_bits_1_da, address_decoder_4_bits_1_db,
       address_decoder_4_bits_1_dc, address_decoder_4_bits_1_dd, address_decoder_4_bits_1_de,
       address_decoder_4_bits_1_df, and_1_out, and_2_out, and_3_out, and_4_out, and_5_out, and_6_out,
       and_7_out, and_8_out, and_9_out, and_10_out, and_11_out, and_12_out, and_13_out, and_14_out,
       and_15_out, and_16_out, and_17_out, and_18_out, and_19_out, and_20_out, and_21_out, and_22_out,
       and_23_out, and_24_out, and_25_out, and_26_out, and_27_out, and_28_out, and_29_out, and_30_out,
       and_31_out, and_32_out, sram_16_bytes_1_o0, sram_16_bytes_1_o1, sram_16_bytes_1_o2,
       sram_16_bytes_1_o3, sram_16_bytes_1_o4, sram_16_bytes_1_o5, sram_16_bytes_1_o6, sram_16_bytes_1_o7;

  Address_Decoder_4_bits address_decoder_4_bits_1 (
    .A3(A7), .A2(A6), .A1(A5), .A0(A4), .Enable(1'b1), .DF(address_decoder_4_bits_1_df),
    .DE(address_decoder_4_bits_1_de), .DD(address_decoder_4_bits_1_dd), .DC(address_decoder_4_bits_1_dc),
    .DB(address_decoder_4_bits_1_db), .DA(address_decoder_4_bits_1_da), .D9(address_decoder_4_bits_1_d9),
    .D8(address_decoder_4_bits_1_d8), .D7(address_decoder_4_bits_1_d7), .D6(address_decoder_4_bits_1_d6),
    .D5(address_decoder_4_bits_1_d5), .D4(address_decoder_4_bits_1_d4), .D3(address_decoder_4_bits_1_d3),
    .D2(address_decoder_4_bits_1_d2), .D1(address_decoder_4_bits_1_d1), .D0(address_decoder_4_bits_1_d0));
  and and_1 (and_1_out, Read, address_decoder_4_bits_1_d0);
  and and_2 (and_2_out, Write, address_decoder_4_bits_1_d0);
  and and_3 (and_3_out, Read, address_decoder_4_bits_1_d1);
  and and_4 (and_4_out, Write, address_decoder_4_bits_1_d1);
  and and_5 (and_5_out, Read, address_decoder_4_bits_1_d2);
  and and_6 (and_6_out, Write, address_decoder_4_bits_1_d2);
  and and_7 (and_7_out, Read, address_decoder_4_bits_1_d3);
  and and_8 (and_8_out, Write, address_decoder_4_bits_1_d3);
  and and_9 (and_9_out, Read, address_decoder_4_bits_1_d4);
  and and_10 (and_10_out, Write, address_decoder_4_bits_1_d4);
  and and_11 (and_11_out, Read, address_decoder_4_bits_1_d5);
  and and_12 (and_12_out, Write, address_decoder_4_bits_1_d5);
  and and_13 (and_13_out, Read, address_decoder_4_bits_1_d6);
  and and_14 (and_14_out, Write, address_decoder_4_bits_1_d6);
  and and_15 (and_15_out, Read, address_decoder_4_bits_1_d7);
  and and_16 (and_16_out, Write, address_decoder_4_bits_1_d7);
  SRAM_16_bytes sram_16_bytes_1 (
    .A3(A3), .A2(A2), .A1(A1), .A0(A0), .Write(and_2_out), .Read(and_1_out), .Clock(Clock), .Clear(Clear),
    .O7(sram_16_bytes_1_o7), .O6(sram_16_bytes_1_o6), .O5(sram_16_bytes_1_o5), .O4(sram_16_bytes_1_o4),
    .O3(sram_16_bytes_1_o3), .O2(sram_16_bytes_1_o2), .O1(sram_16_bytes_1_o1), .O0(sram_16_bytes_1_o0),
    .D7(sram_16_bytes_1_o7), .D6(sram_16_bytes_1_o6), .D5(sram_16_bytes_1_o5), .D4(sram_16_bytes_1_o4),
    .D3(sram_16_bytes_1_o3), .D2(sram_16_bytes_1_o2), .D1(sram_16_bytes_1_o1), .D0(sram_16_bytes_1_o0));
  SRAM_16_bytes sram_16_bytes_2 (
    .A3(A3), .A2(A2), .A1(A1), .A0(A0), .Write(and_4_out), .Read(and_3_out), .Clock(Clock), .Clear(Clear),
    .O7(sram_16_bytes_1_o7), .O6(sram_16_bytes_1_o6), .O5(sram_16_bytes_1_o5), .O4(sram_16_bytes_1_o4),
    .O3(sram_16_bytes_1_o3), .O2(sram_16_bytes_1_o2), .O1(sram_16_bytes_1_o1), .O0(sram_16_bytes_1_o0),
    .D7(sram_16_bytes_1_o7), .D6(sram_16_bytes_1_o6), .D5(sram_16_bytes_1_o5), .D4(sram_16_bytes_1_o4),
    .D3(sram_16_bytes_1_o3), .D2(sram_16_bytes_1_o2), .D1(sram_16_bytes_1_o1), .D0(sram_16_bytes_1_o0));
  SRAM_16_bytes sram_16_bytes_3 (
    .A3(A3), .A2(A2), .A1(A1), .A0(A0), .Write(and_6_out), .Read(and_5_out), .Clock(Clock), .Clear(Clear),
    .O7(sram_16_bytes_1_o7), .O6(sram_16_bytes_1_o6), .O5(sram_16_bytes_1_o5), .O4(sram_16_bytes_1_o4),
    .O3(sram_16_bytes_1_o3), .O2(sram_16_bytes_1_o2), .O1(sram_16_bytes_1_o1), .O0(sram_16_bytes_1_o0),
    .D7(sram_16_bytes_1_o7), .D6(sram_16_bytes_1_o6), .D5(sram_16_bytes_1_o5), .D4(sram_16_bytes_1_o4),
    .D3(sram_16_bytes_1_o3), .D2(sram_16_bytes_1_o2), .D1(sram_16_bytes_1_o1), .D0(sram_16_bytes_1_o0));
  SRAM_16_bytes sram_16_bytes_4 (
    .A3(A3), .A2(A2), .A1(A1), .A0(A0), .Write(and_8_out), .Read(and_7_out), .Clock(Clock), .Clear(Clear),
    .O7(sram_16_bytes_1_o7), .O6(sram_16_bytes_1_o6), .O5(sram_16_bytes_1_o5), .O4(sram_16_bytes_1_o4),
    .O3(sram_16_bytes_1_o3), .O2(sram_16_bytes_1_o2), .O1(sram_16_bytes_1_o1), .O0(sram_16_bytes_1_o0),
    .D7(sram_16_bytes_1_o7), .D6(sram_16_bytes_1_o6), .D5(sram_16_bytes_1_o5), .D4(sram_16_bytes_1_o4),
    .D3(sram_16_bytes_1_o3), .D2(sram_16_bytes_1_o2), .D1(sram_16_bytes_1_o1), .D0(sram_16_bytes_1_o0));
  SRAM_16_bytes sram_16_bytes_5 (
    .A3(A3), .A2(A2), .A1(A1), .A0(A0), .Write(and_10_out), .Read(and_9_out), .Clock(Clock), .Clear(Clear),
    .O7(sram_16_bytes_1_o7), .O6(sram_16_bytes_1_o6), .O5(sram_16_bytes_1_o5), .O4(sram_16_bytes_1_o4),
    .O3(sram_16_bytes_1_o3), .O2(sram_16_bytes_1_o2), .O1(sram_16_bytes_1_o1), .O0(sram_16_bytes_1_o0),
    .D7(sram_16_bytes_1_o7), .D6(sram_16_bytes_1_o6), .D5(sram_16_bytes_1_o5), .D4(sram_16_bytes_1_o4),
    .D3(sram_16_bytes_1_o3), .D2(sram_16_bytes_1_o2), .D1(sram_16_bytes_1_o1), .D0(sram_16_bytes_1_o0));
  SRAM_16_bytes sram_16_bytes_6 (
    .A3(A3), .A2(A2), .A1(A1), .A0(A0), .Write(and_12_out), .Read(and_11_out), .Clock(Clock), .Clear(Clear),
    .O7(sram_16_bytes_1_o7), .O6(sram_16_bytes_1_o6), .O5(sram_16_bytes_1_o5), .O4(sram_16_bytes_1_o4),
    .O3(sram_16_bytes_1_o3), .O2(sram_16_bytes_1_o2), .O1(sram_16_bytes_1_o1), .O0(sram_16_bytes_1_o0),
    .D7(sram_16_bytes_1_o7), .D6(sram_16_bytes_1_o6), .D5(sram_16_bytes_1_o5), .D4(sram_16_bytes_1_o4),
    .D3(sram_16_bytes_1_o3), .D2(sram_16_bytes_1_o2), .D1(sram_16_bytes_1_o1), .D0(sram_16_bytes_1_o0));
  SRAM_16_bytes sram_16_bytes_7 (
    .A3(A3), .A2(A2), .A1(A1), .A0(A0), .Write(and_14_out), .Read(and_13_out), .Clock(Clock), .Clear(Clear),
    .O7(sram_16_bytes_1_o7), .O6(sram_16_bytes_1_o6), .O5(sram_16_bytes_1_o5), .O4(sram_16_bytes_1_o4),
    .O3(sram_16_bytes_1_o3), .O2(sram_16_bytes_1_o2), .O1(sram_16_bytes_1_o1), .O0(sram_16_bytes_1_o0),
    .D7(sram_16_bytes_1_o7), .D6(sram_16_bytes_1_o6), .D5(sram_16_bytes_1_o5), .D4(sram_16_bytes_1_o4),
    .D3(sram_16_bytes_1_o3), .D2(sram_16_bytes_1_o2), .D1(sram_16_bytes_1_o1), .D0(sram_16_bytes_1_o0));
  SRAM_16_bytes sram_16_bytes_8 (
    .A3(A3), .A2(A2), .A1(A1), .A0(A0), .Write(and_16_out), .Read(and_15_out), .Clock(Clock), .Clear(Clear),
    .O7(sram_16_bytes_1_o7), .O6(sram_16_bytes_1_o6), .O5(sram_16_bytes_1_o5), .O4(sram_16_bytes_1_o4),
    .O3(sram_16_bytes_1_o3), .O2(sram_16_bytes_1_o2), .O1(sram_16_bytes_1_o1), .O0(sram_16_bytes_1_o0),
    .D7(sram_16_bytes_1_o7), .D6(sram_16_bytes_1_o6), .D5(sram_16_bytes_1_o5), .D4(sram_16_bytes_1_o4),
    .D3(sram_16_bytes_1_o3), .D2(sram_16_bytes_1_o2), .D1(sram_16_bytes_1_o1), .D0(sram_16_bytes_1_o0));
  assign O5 = Read ? sram_16_bytes_1_o5 : 1'bz;  // Controlled_Buffer controlled_buffer_1
  assign O7 = Read ? sram_16_bytes_1_o7 : 1'bz;  // Controlled_Buffer controlled_buffer_2
  assign O4 = Read ? sram_16_bytes_1_o4 : 1'bz;  // Controlled_Buffer controlled_buffer_3
  assign O6 = Read ? sram_16_bytes_1_o6 : 1'bz;  // Controlled_Buffer controlled_buffer_4
  assign O0 = Read ? sram_16_bytes_1_o0 : 1'bz;  // Controlled_Buffer controlled_buffer_5
  assign O3 = Read ? sram_16_bytes_1_o3 : 1'bz;  // Controlled_Buffer controlled_buffer_6
  assign O1 = Read ? sram_16_bytes_1_o1 : 1'bz;  // Controlled_Buffer controlled_buffer_7
  assign O2 = Read ? sram_16_bytes_1_o2 : 1'bz;  // Controlled_Buffer controlled_buffer_8
  assign sram_16_bytes_1_o6 = Write ? D6 : 1'bz;  // Controlled_Buffer controlled_buffer_9
  assign sram_16_bytes_1_o7 = Write ? D7 : 1'bz;  // Controlled_Buffer controlled_buffer_10
  assign sram_16_bytes_1_o5 = Write ? D5 : 1'bz;  // Controlled_Buffer controlled_buffer_11
  assign sram_16_bytes_1_o1 = Write ? D1 : 1'bz;  // Controlled_Buffer controlled_buffer_12
  assign sram_16_bytes_1_o3 = Write ? D3 : 1'bz;  // Controlled_Buffer controlled_buffer_13
  assign sram_16_bytes_1_o4 = Write ? D4 : 1'bz;  // Controlled_Buffer controlled_buffer_14
  assign sram_16_bytes_1_o2 = Write ? D2 : 1'bz;  // Controlled_Buffer controlled_buffer_15
  SRAM_16_bytes sram_16_bytes_9 (
    .A3(A3), .A2(A2), .A1(A1), .A0(A0), .Write(and_17_out), .Read(and_18_out), .Clock(Clock), .Clear(Clear),
    .O7(sram_16_bytes_1_o7), .O6(sram_16_bytes_1_o6), .O5(sram_16_bytes_1_o5), .O4(sram_16_bytes_1_o4),
    .O3(sram_16_bytes_1_o3), .O2(sram_16_bytes_1_o2), .O1(sram_16_bytes_1_o1), .O0(sram_16_bytes_1_o0),
    .D7(sram_16_bytes_1_o7), .D6(sram_16_bytes_1_o6), .D5(sram_16_bytes_1_o5), .D4(sram_16_bytes_1_o4),
    .D3(sram_16_bytes_1_o3), .D2(sram_16_bytes_1_o2), .D1(sram_16_bytes_1_o1), .D0(sram_16_bytes_1_o0));
  SRAM_16_bytes sram_16_bytes_10 (
    .A3(A3), .A2(A2), .A1(A1), .A0(A0), .Write(and_19_out), .Read(and_20_out), .Clock(Clock), .Clear(Clear),
    .O7(sram_16_bytes_1_o7), .O6(sram_16_bytes_1_o6), .O5(sram_16_bytes_1_o5), .O4(sram_16_bytes_1_o4),
    .O3(sram_16_bytes_1_o3), .O2(sram_16_bytes_1_o2), .O1(sram_16_bytes_1_o1), .O0(sram_16_bytes_1_o0),
    .D7(sram_16_bytes_1_o7), .D6(sram_16_bytes_1_o6), .D5(sram_16_bytes_1_o5), .D4(sram_16_bytes_1_o4),
    .D3(sram_16_bytes_1_o3), .D2(sram_16_bytes_1_o2), .D1(sram_16_bytes_1_o1), .D0(sram_16_bytes_1_o0));
  SRAM_16_bytes sram_16_bytes_11 (
    .A3(A3), .A2(A2), .A1(A1), .A0(A0), .Write(and_21_out), .Read(and_22_out), .Clock(Clock), .Clear(Clear),
    .O7(sram_16_bytes_1_o7), .O6(sram_16_bytes_1_o6), .O5(sram_16_bytes_1_o5), .O4(sram_16_bytes_1_o4),
    .O3(sram_16_bytes_1_o3), .O2(sram_16_bytes_1_o2), .O1(sram_16_bytes_1_o1), .O0(sram_16_bytes_1_o0),
    .D7(sram_16_bytes_1_o7), .D6(sram_16_bytes_1_o6), .D5(sram_16_bytes_1_o5), .D4(sram_16_bytes_1_o4),
    .D3(sram_16_bytes_1_o3), .D2(sram_16_bytes_1_o2), .D1(sram_16_bytes_1_o1), .D0(sram_16_bytes_1_o0));
  SRAM_16_bytes sram_16_bytes_12 (
    .A3(A3), .A2(A2), .A1(A1), .A0(A0), .Write(and_23_out), .Read(and_24_out), .Clock(Clock), .Clear(Clear),
    .O7(sram_16_bytes_1_o7), .O6(sram_16_bytes_1_o6), .O5(sram_16_bytes_1_o5), .O4(sram_16_bytes_1_o4),
    .O3(sram_16_bytes_1_o3), .O2(sram_16_bytes_1_o2), .O1(sram_16_bytes_1_o1), .O0(sram_16_bytes_1_o0),
    .D7(sram_16_bytes_1_o7), .D6(sram_16_bytes_1_o6), .D5(sram_16_bytes_1_o5), .D4(sram_16_bytes_1_o4),
    .D3(sram_16_bytes_1_o3), .D2(sram_16_bytes_1_o2), .D1(sram_16_bytes_1_o1), .D0(sram_16_bytes_1_o0));
  SRAM_16_bytes sram_16_bytes_13 (
    .A3(A3), .A2(A2), .A1(A1), .A0(A0), .Write(and_25_out), .Read(and_26_out), .Clock(Clock), .Clear(Clear),
    .O7(sram_16_bytes_1_o7), .O6(sram_16_bytes_1_o6), .O5(sram_16_bytes_1_o5), .O4(sram_16_bytes_1_o4),
    .O3(sram_16_bytes_1_o3), .O2(sram_16_bytes_1_o2), .O1(sram_16_bytes_1_o1), .O0(sram_16_bytes_1_o0),
    .D7(sram_16_bytes_1_o7), .D6(sram_16_bytes_1_o6), .D5(sram_16_bytes_1_o5), .D4(sram_16_bytes_1_o4),
    .D3(sram_16_bytes_1_o3), .D2(sram_16_bytes_1_o2), .D1(sram_16_bytes_1_o1), .D0(sram_16_bytes_1_o0));
  SRAM_16_bytes sram_16_bytes_14 (
    .A3(A3), .A2(A2), .A1(A1), .A0(A0), .Write(and_27_out), .Read(and_28_out), .Clock(Clock), .Clear(Clear),
    .O7(sram_16_bytes_1_o7), .O6(sram_16_bytes_1_o6), .O5(sram_16_bytes_1_o5), .O4(sram_16_bytes_1_o4),
    .O3(sram_16_bytes_1_o3), .O2(sram_16_bytes_1_o2), .O1(sram_16_bytes_1_o1), .O0(sram_16_bytes_1_o0),
    .D7(sram_16_bytes_1_o7), .D6(sram_16_bytes_1_o6), .D5(sram_16_bytes_1_o5), .D4(sram_16_bytes_1_o4),
    .D3(sram_16_bytes_1_o3), .D2(sram_16_bytes_1_o2), .D1(sram_16_bytes_1_o1), .D0(sram_16_bytes_1_o0));
  SRAM_16_bytes sram_16_bytes_15 (
    .A3(A3), .A2(A2), .A1(A1), .A0(A0), .Write(and_29_out), .Read(and_30_out), .Clock(Clock), .Clear(Clear),
    .O7(sram_16_bytes_1_o7), .O6(sram_16_bytes_1_o6), .O5(sram_16_bytes_1_o5), .O4(sram_16_bytes_1_o4),
    .O3(sram_16_bytes_1_o3), .O2(sram_16_bytes_1_o2), .O1(sram_16_bytes_1_o1), .O0(sram_16_bytes_1_o0),
    .D7(sram_16_bytes_1_o7), .D6(sram_16_bytes_1_o6), .D5(sram_16_bytes_1_o5), .D4(sram_16_bytes_1_o4),
    .D3(sram_16_bytes_1_o3), .D2(sram_16_bytes_1_o2), .D1(sram_16_bytes_1_o1), .D0(sram_16_bytes_1_o0));
  SRAM_16_bytes sram_16_bytes_16 (
    .A3(A3), .A2(A2), .A1(A1), .A0(A0), .Write(and_31_out), .Read(and_32_out), .Clock(Clock), .Clear(Clear),
    .O7(sram_16_bytes_1_o7), .O6(sram_16_bytes_1_o6), .O5(sram_16_bytes_1_o5), .O4(sram_16_bytes_1_o4),
    .O3(sram_16_bytes_1_o3), .O2(sram_16_bytes_1_o2), .O1(sram_16_bytes_1_o1), .O0(sram_16_bytes_1_o0),
    .D7(sram_16_bytes_1_o7), .D6(sram_16_bytes_1_o6), .D5(sram_16_bytes_1_o5), .D4(sram_16_bytes_1_o4),
    .D3(sram_16_bytes_1_o3), .D2(sram_16_bytes_1_o2), .D1(sram_16_bytes_1_o1), .D0(sram_16_bytes_1_o0));
  assign sram_16_bytes_1_o0 = Write ? D0 : 1'bz;  // Controlled_Buffer controlled_buffer_16
  and and_17 (and_17_out, Write, address_decoder_4_bits_1_df);
  and and_18 (and_18_out, Read, address_decoder_4_bits_1_df);
  and and_19 (and_19_out, Write, address_decoder_4_bits_1_de);
  and and_20 (and_20_out, Read, address_decoder_4_bits_1_de);
  and and_21 (and_21_out, Write, address_decoder_4_bits_1_dd);
  and and_22 (and_22_out, Read, address_decoder_4_bits_1_dd);
  and and_23 (and_23_out, Write, address_decoder_4_bits_1_dc);
  and and_24 (and_24_out, Read, address_decoder_4_bits_1_dc);
  and and_25 (and_25_out, Write, address_decoder_4_bits_1_db);
  and and_26 (and_26_out, Read, address_decoder_4_bits_1_db);
  and and_27 (and_27_out, Write, address_decoder_4_bits_1_d8);
  and and_28 (and_28_out, Read, address_decoder_4_bits_1_d8);
  and and_29 (and_29_out, Write, address_decoder_4_bits_1_d9);
  and and_30 (and_30_out, Read, address_decoder_4_bits_1_d9);
  and and_31 (and_31_out, Write, address_decoder_4_bits_1_da);
  and and_32 (and_32_out, Read, address_decoder_4_bits_1_da);
endmodule
